# Fritzing sketch AR08a_R (saved by Fritzing 0.9.3b)
breadboards: 1

parts:
  부품2 = Arduino Uno (Rev3)
  R1 = Resistor [tolerance=±5% resistance=220 package=THT]

nets:
  N1: 부품2.5V, R1.Pin_1
  N2: 부품2.GND, R1.Pin_0
