# Fritzing sketch AR08_4led (saved by Fritzing 0.9.3b)
breadboards: 1

parts:
  부품1 = Arduino Uno (Rev3) - ICSP
  LED2 = LED - 5mm [color="Red (633nm)" package="5 mm [THT]"]
  R1 = Resistor [tolerance=±5% resistance=250 package=THT]
  R2 = Resistor [tolerance=±5% resistance=250 package=THT]
  LED3 = LED - 5mm [color="Red (633nm)" package="5 mm [THT]"]
  LED4 = LED - 5mm [color="Red (633nm)" package="5 mm [THT]"]
  LED5 = LED - 5mm [color="Red (633nm)" package="5 mm [THT]"]
  R3 = Resistor [tolerance=±5% resistance=250 package=THT]
  R4 = Resistor [tolerance=±5% resistance=250 package=THT]

nets:
  N1: 부품1.D9_PWM, LED4.cathode
  N2: 부품1.D3_PWM, LED2.cathode
  N3: 부품1.D6_PWM, LED5.cathode
  N4: R1.Pin_0, LED3.anode
  N5: R1.Pin_1, R2.Pin_1, R3.Pin_1, R4.Pin_1
  N6: LED4.anode, R4.Pin_0
  N7: LED5.anode, R3.Pin_0
